# Fritzing sketch ArduinoNano (saved by Fritzing 0.9.3b)
breadboards: 1

parts:
  Componente1 = Arduino Nano (Rev3.0)
  R1 = Resistor [tolerance=±5% resistance=4.7k package=THT]
  IC2 = IC, DIP package, 8 pins [chip_label=X9C103]
  R2 = Resistor [tolerance=±5% resistance=33k package=THT]
  Q1 = NPN-Transistor [package="TO92 [THT]"]
  IC1 = IC, DIP package, 8 pins [chip_label=X9C103]
  R3 = Resistor [tolerance=±5% resistance=100 package=THT]  # not connected

nets (from the schematic view):
  N1: Componente1.GND, IC2.pin4, Q1.E, IC1.pin4
  N2: Componente1.D2, IC2.pin1
  N3: Componente1.D3, IC2.pin2
  N4: Componente1.D4, IC2.pin7
  N5: Componente1.D5, R1.Pin_1
  N6: Componente1.D6, IC1.pin3, IC1.pin5
  N7: Componente1.D8, IC1.pin1
  N8: Componente1.D9, IC1.pin2
  N9: Componente1.D10, IC1.pin7
  N10: Componente1.5V, Componente1.A3, IC2.pin8, IC1.pin8
  N11: Componente1.A1, R2.Pin_0, Q1.B
  N12: R1.Pin_0, R2.Pin_1
  N13: IC2.pin3, IC2.pin5
  N14: IC2.pin6, Q1.C

notes:
  Trazador de curvas de un BJT 547B.
