# Fritzing sketch ArduinoUno (saved by Fritzing 0.9.3b)
breadboards: 1

parts:
  R1 = Resistor [tolerance=±5% resistance=4.7k package=THT]
  IC2 = IC, DIP package, 8 pins [chip_label=X9C103]
  R2 = Resistor [tolerance=±5% resistance=33k package=THT]
  Q1 = NPN-Transistor [package="TO92 [THT]"]
  IC1 = IC, DIP package, 8 pins [chip_label=X9C103]
  R3 = Resistor [tolerance=±5% resistance=100 package=THT]
  Componente2 = Arduino Uno (Rev3)

nets (from the breadboard view):
  N1: R1.Pin_0, R2.Pin_1, IC1.pin6, Componente2.A0
  N2: R1.Pin_1, Componente2.D5_PWM
  N3: IC2.pin1, Componente2.D2
  N4: IC2.pin2, Componente2.D3_PWM
  N5: IC2.pin3, IC2.pin5
  N6: IC2.pin4, Q1.E, IC1.pin4, Componente2.GND
  N7: IC2.pin6, R3.Pin_1, Componente2.A3
  N8: IC2.pin7, Componente2.D4
  N9: IC2.pin8, IC1.pin8, Componente2.5V
  N10: R2.Pin_0, Q1.B, Componente2.A1
  N11: Q1.C, R3.Pin_0, Componente2.A2
  N12: IC1.pin1, Componente2.D8
  N13: IC1.pin2, Componente2.D9_PWM
  N14: IC1.pin3, IC1.pin5, Componente2.D6_PWM
  N15: IC1.pin7, Componente2.D10_PWM/SS

notes:
  Trazador de curvas de un BJT 547B.
