# Fritzing sketch DDS (saved by Fritzing 0.9.3b)
breadboards: 1

parts:
  Componente1 = Arduino Nano (Rev3.0)
  U1 = 555 Timer [package="DIP8 [THT]"]
  U2 = SN74LS04N [package="DIP14 [THT]"]
  U3 = CD4015B [package=dil16]
  R1 = Resistor [tolerance=±5% resistance=1k package=THT]
  R2 = Resistor [tolerance=±5% resistance=10k package=THT]
  C1 = Electrolytic Capacitor [capacitance=10µF voltage=20V package="100 mil [THT, electrolytic]"]
  R4 = Resistor [tolerance=±5% resistance=47k package=THT]
  R3 = Resistor [tolerance=±5% resistance=47k package=THT]
  R5 = Resistor [tolerance=±5% resistance=33k package=THT]
  R6 = Resistor [tolerance=±5% resistance=33k package=THT]
  R7 = Resistor [tolerance=±5% resistance=4.7 package=THT]
  R8 = Resistor [tolerance=±5% resistance=4.7 package=THT]
  R9 = Resistor [tolerance=±5% resistance=22k package=THT]
  R10 = Resistor [tolerance=±5% resistance=22k package=THT]
  R11 = Resistor [tolerance=±5% resistance=100k package=THT]
  R12 = Resistor [tolerance=±5% resistance=10k package=THT]
  R13 = Resistor [tolerance=±5% resistance=10k package=THT]
  R14 = Resistor [tolerance=±5% resistance=100k package=THT]
  R15 = Resistor [tolerance=±5% resistance=10k package=THT]
  R16 = Resistor [tolerance=±5% resistance=10k package=THT]
  R17 = Resistor [tolerance=±5% resistance=100k package=THT]
  C2 = Electrolytic Capacitor [capacitance=1µF package="100 mil [THT, electrolytic]"]

nets:
  GND: Componente1.GND, U1.Ground, U2.GND, U3.GND, C1.-, R17.Pin_1
  N1: Componente1.D2, U1.Output
  5V: Componente1.5V, U1.Reset, U1.Vcc_Supply_Voltage, U2.Vcc, C2.+
  N2: Componente1.A0, R4.Pin_1, R3.Pin_0, R5.Pin_0, R6.Pin_1, R9.Pin_1, R10.Pin_0, R13.Pin_0, R16.Pin_0
  N3: U1.Trigger, U1.Threshold, U3.Y0, U3.B, R2.Pin_0, C1.+
  N4: U1.Discharge, R1.Pin_1, R2.Pin_1
  N5: U2.2B, U3.Y2, R14.Pin_1
  N6: U2.2Y, U3.VEE
  N7: U3.Y, R6.Pin_0
  N8: U3.Y3, R4.Pin_0
  N9: U3.Y1, R11.Pin_0
  N10: U3.INH, U3.X1, R17.Pin_0, C2.-
  N11: U3.A, R7.Pin_0
  N12: U3.X3, R3.Pin_1
  N13: U3.X0, R5.Pin_1
  N14: U3.X, R8.Pin_1
  N15: R7.Pin_1, R9.Pin_0
  N16: R8.Pin_0, R10.Pin_1
  N17: R11.Pin_1, R12.Pin_1
  N18: R12.Pin_0, R13.Pin_1
  N19: R14.Pin_0, R15.Pin_1
  N20: R15.Pin_0, R16.Pin_1

custom parts:
  SN74LS04N: Quad 2-input positive-OR gates
  CD4015B: Dual 4:1 analog mux
